// Logisim project project.circ as structural Verilog: 18 circuits, main circuit main
module main (
  input  in_1
);

  wire alu_1_aout0, alu_1_aout1, alu_1_aout2, alu_1_aout3, alu_1_negative, alu_1_overflow,
       alu_1_signed_overflow, alu_1_zero, ALUop, ALUrun, and_1_out, and_2_out, aout_1_b0, aout_1_b1,
       aout_1_b2, aout_1_b3, AOUTo, CLK, clock_1_out, cu_1_cuadr, cu_1_rammode, d_1_a, d_1_b, d_1_c, d_1_dd,
       d_1_e, d_1_f, d_1_g, d_1_l_b, d_1_l_c, HALT, ir_1_b0, ir_1_b1, ir_1_b2, ir_1_b3, IRi, IRo, l_1_b0,
       l_1_b1, l_1_b2, l_1_b3, Li, mar_1_b0, mar_1_b1, mar_1_b2, MARi, MARo, mbr_1_b0, mbr_1_b1, mbr_1_b2,
       mbr_1_b3, MBRi, MBRo, not_1_out, or_1_out, or_2_out, or_3_out, or_4_out, or_5_out, or_6_out, or_7_out,
       or_8_out, or_9_out, or_10_out, or_11_out, or_12_out, or_13_out, or_14_out, or_15_out, or_16_out,
       or_17_out, or_18_out, or_19_out, or_20_out, or_21_out, or_22_out, or_23_out, or_24_out, or_25_out,
       or_26_out, or_27_out, or_28_out, or_29_out, or_30_out, or_31_out, or_32_out, pc_1_b0, pc_1_b1,
       pc_1_b2, PCi, pcincrementor_1_pc0, pcincrementor_1_pc1, pcincrementor_1_pc2, PCo, r0_1_b0, r0_1_b1,
       r0_1_b2, r0_1_b3, R0i, R0o, r1_1_b0, r1_1_b1, r1_1_b2, r1_1_b3, R1i, R1o, r_1_b0, r_1_b1, r_1_b2,
       r_1_b3, ramcircuit_1_dro0, ramcircuit_1_dro1, ramcircuit_1_dro2, ramcircuit_1_dro3, ramcircuit_1_x0,
       ramcircuit_1_x1, ramcircuit_1_x2, ramcircuit_1_x3, RAMrun, Ri, status_1_b0, status_1_b1, status_1_b2,
       status_1_b3;

  R0 r0_1 (
    .b3(r0_1_b3), .b2(r0_1_b2), .b1(r0_1_b1), .b0(r0_1_b0), .d0(or_32_out), .o(R0o), .clk(CLK), .i(R0i),
    .d3(or_29_out), .d2(or_30_out), .d1(or_31_out));
  or or_1 (or_1_out, r0_1_b3, 1'b0);
  or or_2 (or_2_out, r0_1_b2, 1'b0);
  or or_3 (or_3_out, r0_1_b1, 1'b0);
  or or_4 (or_4_out, r0_1_b0, 1'b0);
  R1 r1_1 (
    .d3(or_29_out), .d2(or_30_out), .d1(or_31_out), .d0(or_32_out), .o(R1o), .clk(CLK), .i(R1i),
    .b3(r1_1_b3), .b2(r1_1_b2), .b1(r1_1_b1), .b0(r1_1_b0));
  or or_5 (or_5_out, r1_1_b3, or_1_out);
  or or_6 (or_6_out, r1_1_b2, or_2_out);
  or or_7 (or_7_out, r1_1_b1, or_3_out);
  or or_8 (or_8_out, r1_1_b0, or_4_out);
  L l_1 (
    .d3(or_29_out), .d2(or_30_out), .d1(or_31_out), .d0(or_32_out), .o(ALUrun), .clk(CLK), .i(Li),
    .b3(l_1_b3), .b2(l_1_b2), .b1(l_1_b1), .b0(l_1_b0));
  R r_1 (
    .d3(or_29_out), .d2(or_30_out), .d1(or_31_out), .d0(or_32_out), .o(ALUrun), .clk(CLK), .i(Ri),
    .b3(r_1_b3), .b2(r_1_b2), .b1(r_1_b1), .b0(r_1_b0));
  and and_1 (and_1_out, CLK, ALUrun);
  ALU alu_1 (
    .L3(l_1_b3), .L2(l_1_b2), .L1(l_1_b1), .L0(l_1_b0), .R3(r_1_b3), .R2(r_1_b2), .R1(r_1_b1), .R0(r_1_b0),
    .clk(and_1_out), .AddSub(ALUop), .signed_overflow(alu_1_signed_overflow), .overflow(alu_1_overflow),
    .zero(alu_1_zero), .negative(alu_1_negative), .Aout3(alu_1_aout3), .Aout2(alu_1_aout2),
    .Aout1(alu_1_aout1), .Aout0(alu_1_aout0));
  // Probe on in_1
  Aout aout_1 (
    .d3(alu_1_aout3), .d2(alu_1_aout2), .d1(alu_1_aout1), .d0(alu_1_aout0), .o(AOUTo), .clk(CLK), .i(ALUrun),
    .b3(aout_1_b3), .b2(aout_1_b2), .b1(aout_1_b1), .b0(aout_1_b0));
  or or_9 (or_9_out, aout_1_b3, or_5_out);
  or or_10 (or_10_out, aout_1_b2, or_6_out);
  or or_11 (or_11_out, aout_1_b1, or_7_out);
  or or_12 (or_12_out, aout_1_b0, or_8_out);
  Status status_1 (
    .d3(alu_1_signed_overflow), .d2(alu_1_overflow), .d1(alu_1_zero), .d0(alu_1_negative), .o(1'b0),
    .clk(CLK), .i(ALUrun), .b3(status_1_b3), .b2(status_1_b2), .b1(status_1_b1), .b0(status_1_b0));
  or or_13 (or_13_out, status_1_b3, or_9_out);
  or or_14 (or_14_out, status_1_b2, or_10_out);
  or or_15 (or_15_out, status_1_b1, or_11_out);
  or or_16 (or_16_out, status_1_b0, or_12_out);
  MBR mbr_1 (
    .d3(or_29_out), .d2(or_30_out), .d1(or_31_out), .d0(or_32_out), .o(MBRo), .clk(CLK), .i(MBRi),
    .b3(mbr_1_b3), .b2(mbr_1_b2), .b1(mbr_1_b1), .b0(mbr_1_b0));
  or or_17 (or_17_out, mbr_1_b3, or_13_out);
  or or_18 (or_18_out, mbr_1_b2, or_14_out);
  or or_19 (or_19_out, mbr_1_b1, or_15_out);
  or or_20 (or_20_out, mbr_1_b0, or_16_out);
  IR ir_1 (
    .d3(mbr_1_b3), .d2(mbr_1_b2), .d1(mbr_1_b1), .d0(mbr_1_b0), .o(IRo), .clk(CLK), .i(IRi), .b3(ir_1_b3),
    .b2(ir_1_b2), .b1(ir_1_b1), .b0(ir_1_b0));
  CU cu_1 (
    .ir3(ir_1_b3), .ir2(ir_1_b2), .ir1(ir_1_b1), .ir0(ir_1_b0), .clk(CLK), .HALT(HALT), .PCi(PCi), .PCo(PCo),
    .RAMmode(cu_1_rammode), .RAMrun(RAMrun), .MARi(MARi), .MARo(MARo), .MBRi(MBRi), .MBRo(MBRo), .IRi(IRi),
    .IRo(IRo), .R0i(R0i), .R0o(R0o), .R1i(R1i), .R1o(R1o), .Li(Li), .Ri(Ri), .ALUop(ALUop), .ALUrun(ALUrun),
    .AOUTo(AOUTo), .CUadr(cu_1_cuadr));
  or or_21 (or_21_out, cu_1_rammode, 1'b0);
  or or_22 (or_22_out, cu_1_cuadr, 1'b0);
  PC pc_1 (
    .d2(pcincrementor_1_pc2), .d1(pcincrementor_1_pc1), .d0(pcincrementor_1_pc0), .o(PCo), .clk(CLK),
    .i(PCi), .b2(pc_1_b2), .b1(pc_1_b1), .b0(pc_1_b0));
  PCincrementor pcincrementor_1 (
    .b2(pc_1_b2), .b1(pc_1_b1), .b0(pc_1_b0), .pc2(pcincrementor_1_pc2), .pc1(pcincrementor_1_pc1),
    .pc0(pcincrementor_1_pc0));
  or or_23 (or_23_out, pc_1_b2, or_26_out);
  or or_24 (or_24_out, pc_1_b1, or_27_out);
  or or_25 (or_25_out, pc_1_b0, or_28_out);
  MAR mar_1 (
    .d2(or_23_out), .d1(or_24_out), .d0(or_25_out), .o(MARo), .clk(CLK), .i(MARi), .b2(mar_1_b2),
    .b1(mar_1_b1), .b0(mar_1_b0));
  or or_26 (or_26_out, mar_1_b2, 1'b0);
  or or_27 (or_27_out, mar_1_b1, 1'b0);
  or or_28 (or_28_out, mar_1_b0, or_22_out);
  and and_2 (and_2_out, RAMrun, CLK);
  RamCircuit ramcircuit_1 (
    .clk(and_2_out), .AR2(or_26_out), .AR1(or_27_out), .AR0(or_28_out), .DR3(or_29_out), .DR2(or_30_out),
    .DR1(or_31_out), .DR0(or_32_out), .mode(or_21_out), .DRo3(ramcircuit_1_dro3), .DRo2(ramcircuit_1_dro2),
    .DRo1(ramcircuit_1_dro1), .DRo0(ramcircuit_1_dro0), .X3(ramcircuit_1_x3), .X2(ramcircuit_1_x2),
    .X1(ramcircuit_1_x1), .X0(ramcircuit_1_x0));
  or or_29 (or_29_out, ramcircuit_1_dro3, or_17_out);
  or or_30 (or_30_out, ramcircuit_1_dro2, or_18_out);
  or or_31 (or_31_out, ramcircuit_1_dro1, or_19_out);
  or or_32 (or_32_out, ramcircuit_1_dro0, or_20_out);
  Clock clock_1 (.out(clock_1_out));
  not not_1 (not_1_out, HALT);
  and and_3 (CLK, clock_1_out, not_1_out);
  D d_1 (
    .d3(ramcircuit_1_x3), .d2(ramcircuit_1_x2), .d1(ramcircuit_1_x1), .d0(ramcircuit_1_x0), .clk(CLK),
    .l_b(d_1_l_b), .l_c(d_1_l_c), .a(d_1_a), .b(d_1_b), .c(d_1_c), .dd(d_1_dd), .e(d_1_e), .f(d_1_f),
    .g(d_1_g));
  _7_Segment_Display u_7_segment_display_1 (.b(d_1_l_b), .c(d_1_l_c));  // open: g, f, a, e, d, dp
  _7_Segment_Display u_7_segment_display_2 (
    .g(d_1_g), .f(d_1_f), .a(d_1_a), .b(d_1_b), .e(d_1_e), .d(d_1_dd), .c(d_1_c));  // open: dp

  // Notes on the sheet:
  //   An Ni Xu 261053392, Nancy Tian 261033485
endmodule

module RamCircuit (
  input  clk,
  input  AR2,
  input  AR1,
  input  AR0,
  input  DR3,
  input  DR2,
  input  DR1,
  input  DR0,
  input  mode,
  output DRo3,
  output DRo2,
  output DRo1,
  output DRo0,
  output X3,
  output X2,
  output X1,
  output X0
);

  wire and_1_out, and_2_out, and_3_out, and_4_out, and_5_out, and_6_out, and_7_out, and_8_out, and_9_out,
       and_10_out, and_11_out, and_12_out, and_13_out, and_14_out, and_15_out, and_16_out, and_17_out,
       and_18_out, and_19_out, and_20_out, and_21_out, and_22_out, and_23_out, and_24_out, and_25_out,
       and_26_out, and_27_out, and_28_out, and_29_out, and_30_out, and_31_out, and_32_out, and_33_out,
       and_34_out, and_35_out, and_36_out, and_37_out, and_38_out, and_39_out, and_40_out, and_41_out,
       and_42_out, and_43_out, and_44_out, and_45_out, and_46_out, and_47_out, and_48_out, and_49_out,
       and_50_out, and_51_out, and_52_out, and_53_out, and_54_out, and_55_out, and_56_out, and_57_out,
       and_58_out, and_59_out, and_60_out, and_61_out, and_62_out, and_63_out, and_64_out, and_66_out,
       and_67_out, and_68_out, and_69_out, and_70_out, and_71_out, and_72_out, and_73_out, and_75_out,
       and_76_out, and_77_out, and_78_out, and_79_out, and_80_out, and_81_out, and_82_out, d_ff_1_q,
       d_ff_2_q, d_ff_3_q, d_ff_4_q, d_ff_5_q, d_ff_6_q, d_ff_7_q, d_ff_8_q, d_ff_9_q, d_ff_10_q, d_ff_12_q,
       d_ff_13_q, d_ff_14_q, d_ff_15_q, d_ff_16_q, d_ff_17_q, d_ff_18_q, d_ff_19_q, d_ff_20_q, d_ff_22_q,
       d_ff_23_q, d_ff_24_q, d_ff_25_q, d_ff_26_q, d_ff_27_q, d_ff_28_q, d_ff_29_q, d_ff_30_q, d_ff_31_q,
       d_ff_32_q, d_ff_33_q, d_ff_34_q, d_ff_36_q, d_ff_37_q, d_ff_38_q, d_ff_39_q, d_ff_40_q, d_ff_41_q,
       d_ff_42_q, not_1_out, not_2_out, not_3_out, not_4_out, not_5_out, not_6_out, not_7_out, not_8_out,
       not_9_out, not_10_out, not_11_out, not_12_out, not_13_out, or_1_out, or_2_out, or_3_out, or_4_out;

  D_Flip_Flop #(.trigger("falling")) d_ff_1 (.D(AR2), .clk(clk), .Q(d_ff_1_q));  // open: Qn, preset, reset
  D_Flip_Flop #(.trigger("falling")) d_ff_2 (.D(AR1), .clk(clk), .Q(d_ff_2_q));  // open: Qn, preset, reset
  not not_1 (not_1_out, d_ff_3_q);
  not not_2 (not_2_out, d_ff_2_q);
  not not_3 (not_3_out, d_ff_2_q);
  not not_4 (not_4_out, d_ff_3_q);
  not not_5 (not_5_out, d_ff_1_q);
  not not_6 (not_6_out, d_ff_1_q);
  not not_7 (not_7_out, d_ff_3_q);
  not not_8 (not_8_out, d_ff_1_q);
  not not_9 (not_9_out, d_ff_2_q);
  not not_10 (not_10_out, d_ff_1_q);
  not not_11 (not_11_out, d_ff_2_q);
  not not_12 (not_12_out, d_ff_3_q);
  D_Flip_Flop #(.trigger("falling")) d_ff_3 (.D(AR0), .clk(clk), .Q(d_ff_3_q));  // open: Qn, preset, reset
  and and_1 (and_1_out, d_ff_1_q, d_ff_2_q, clk, d_ff_3_q);
  and and_2 (and_2_out, d_ff_1_q, d_ff_2_q, clk, not_1_out);
  and and_3 (and_3_out, d_ff_1_q, not_2_out, clk, d_ff_3_q);
  and and_4 (and_4_out, d_ff_1_q, not_3_out, clk, not_4_out);
  and and_5 (and_5_out, not_5_out, d_ff_2_q, clk, d_ff_3_q);
  and and_6 (and_6_out, not_6_out, d_ff_2_q, clk, not_7_out);
  and and_7 (and_7_out, not_8_out, not_9_out, clk, d_ff_3_q);
  and and_8 (and_8_out, not_10_out, not_11_out, clk, not_12_out);
  and and_9 (and_9_out, and_1_out, not_13_out);
  and and_10 (and_10_out, and_2_out, not_13_out);
  and and_11 (and_11_out, and_3_out, not_13_out);
  and and_12 (and_12_out, and_4_out, not_13_out);
  and and_13 (and_13_out, and_5_out, not_13_out);
  and and_14 (and_14_out, and_6_out, not_13_out);
  and and_15 (and_15_out, and_7_out, not_13_out);
  and and_16 (and_16_out, and_8_out, not_13_out);
  not not_13 (not_13_out, mode);
  and and_17 (and_17_out, and_1_out, not_13_out, d_ff_12_q);
  D_Flip_Flop #(.trigger("high")) d_ff_4 (.D(and_17_out), .clk(and_9_out), .Q(d_ff_4_q));  // open: Qn, preset, reset
  and and_18 (and_18_out, and_2_out, not_13_out, d_ff_12_q);
  D_Flip_Flop #(.trigger("high")) d_ff_5 (.D(and_18_out), .clk(and_10_out), .Q(d_ff_5_q));  // open: Qn, preset, reset
  and and_19 (and_19_out, and_3_out, not_13_out, d_ff_12_q);
  D_Flip_Flop #(.trigger("high")) d_ff_6 (.D(and_19_out), .clk(and_11_out), .Q(d_ff_6_q));  // open: Qn, preset, reset
  and and_20 (and_20_out, and_4_out, not_13_out, d_ff_12_q);
  D_Flip_Flop #(.trigger("high")) d_ff_7 (.D(and_20_out), .clk(and_12_out), .Q(d_ff_7_q));  // open: Qn, preset, reset
  and and_21 (and_21_out, and_5_out, not_13_out, d_ff_12_q);
  D_Flip_Flop #(.trigger("high")) d_ff_8 (.D(and_21_out), .clk(and_13_out), .Q(d_ff_8_q));  // open: Qn, preset, reset
  and and_22 (and_22_out, and_6_out, not_13_out, d_ff_12_q);
  D_Flip_Flop #(.trigger("high")) d_ff_9 (.D(and_22_out), .clk(and_14_out), .Q(d_ff_9_q));  // open: Qn, preset, reset
  and and_23 (and_23_out, and_7_out, not_13_out, d_ff_12_q);
  D_Flip_Flop #(.trigger("high")) d_ff_10 (.D(and_23_out), .clk(and_15_out), .Q(d_ff_10_q));  // open: Qn, preset, reset
  and and_24 (and_24_out, and_8_out, not_13_out, d_ff_12_q);
  D_Flip_Flop #(.trigger("high")) d_ff_11 (.D(and_24_out), .clk(and_16_out), .Q(X3));  // open: Qn, preset, reset
  or or_1 (or_1_out, and_25_out, and_26_out, and_27_out, and_28_out, and_29_out, and_30_out, and_31_out, and_32_out);
  and and_25 (and_25_out, d_ff_4_q, and_1_out, mode);
  and and_26 (and_26_out, d_ff_5_q, and_2_out, mode);
  and and_27 (and_27_out, d_ff_6_q, and_3_out, mode);
  and and_28 (and_28_out, d_ff_7_q, and_4_out, mode);
  and and_29 (and_29_out, d_ff_8_q, and_5_out, mode);
  and and_30 (and_30_out, d_ff_9_q, and_6_out, mode);
  and and_31 (and_31_out, d_ff_10_q, and_7_out, mode);
  and and_32 (and_32_out, X3, and_8_out, mode);
  D_Flip_Flop #(.trigger("falling")) d_ff_12 (.D(DR3), .clk(clk), .Q(d_ff_12_q));  // open: Qn, preset, reset
  D_Flip_Flop #(.trigger("falling")) d_ff_13 (.D(DR2), .clk(clk), .Q(d_ff_13_q));  // open: Qn, preset, reset
  and and_33 (and_33_out, and_1_out, not_13_out, d_ff_13_q);
  D_Flip_Flop #(.trigger("high")) d_ff_14 (.D(and_33_out), .clk(and_9_out), .Q(d_ff_14_q));  // open: Qn, preset, reset
  and and_34 (and_34_out, and_2_out, not_13_out, d_ff_13_q);
  D_Flip_Flop #(.trigger("high")) d_ff_15 (.D(and_34_out), .clk(and_10_out), .Q(d_ff_15_q));  // open: Qn, preset, reset
  and and_35 (and_35_out, and_3_out, not_13_out, d_ff_13_q);
  D_Flip_Flop #(.trigger("high")) d_ff_16 (.D(and_35_out), .clk(and_11_out), .Q(d_ff_16_q));  // open: Qn, preset, reset
  and and_36 (and_36_out, and_4_out, not_13_out, d_ff_13_q);
  D_Flip_Flop #(.trigger("high")) d_ff_17 (.D(and_36_out), .clk(and_12_out), .Q(d_ff_17_q));  // open: Qn, preset, reset
  and and_37 (and_37_out, and_5_out, not_13_out, d_ff_13_q);
  D_Flip_Flop #(.trigger("high")) d_ff_18 (.D(and_37_out), .clk(and_13_out), .Q(d_ff_18_q));  // open: Qn, preset, reset
  and and_38 (and_38_out, and_6_out, not_13_out, d_ff_13_q);
  D_Flip_Flop #(.trigger("high")) d_ff_19 (.D(and_38_out), .clk(and_14_out), .Q(d_ff_19_q));  // open: Qn, preset, reset
  and and_39 (and_39_out, and_7_out, not_13_out, d_ff_13_q);
  D_Flip_Flop #(.trigger("high")) d_ff_20 (.D(and_39_out), .clk(and_15_out), .Q(d_ff_20_q));  // open: Qn, preset, reset
  and and_40 (and_40_out, and_8_out, not_13_out, d_ff_13_q);
  D_Flip_Flop #(.trigger("high")) d_ff_21 (.D(and_40_out), .clk(and_16_out), .Q(X2));  // open: Qn, preset, reset
  D_Flip_Flop #(.trigger("falling")) d_ff_22 (.D(DR1), .clk(clk), .Q(d_ff_22_q));  // open: Qn, preset, reset
  D_Flip_Flop #(.trigger("high")) d_ff_23 (.D(or_1_out), .clk(clk), .Q(d_ff_23_q));  // open: Qn, preset, reset
  and and_41 (and_41_out, d_ff_14_q, and_1_out, mode);
  and and_42 (and_42_out, d_ff_15_q, and_2_out, mode);
  and and_43 (and_43_out, d_ff_16_q, and_3_out, mode);
  and and_44 (and_44_out, d_ff_17_q, and_4_out, mode);
  and and_45 (and_45_out, d_ff_18_q, and_5_out, mode);
  and and_46 (and_46_out, d_ff_19_q, and_6_out, mode);
  and and_47 (and_47_out, d_ff_20_q, and_7_out, mode);
  and and_48 (and_48_out, X2, and_8_out, mode);
  D_Flip_Flop #(.trigger("falling")) d_ff_24 (.D(DR0), .clk(clk), .Q(d_ff_24_q));  // open: Qn, preset, reset
  D_Flip_Flop #(.trigger("high")) d_ff_25 (.D(or_2_out), .clk(clk), .Q(d_ff_25_q));  // open: Qn, preset, reset
  or or_2 (or_2_out, and_41_out, and_42_out, and_43_out, and_44_out, and_45_out, and_46_out, and_47_out, and_48_out);
  D_Flip_Flop #(.trigger("high")) d_ff_26 (.D(or_3_out), .clk(clk), .Q(d_ff_26_q));  // open: Qn, preset, reset
  D_Flip_Flop #(.trigger("high")) d_ff_27 (.D(or_4_out), .clk(clk), .Q(d_ff_27_q));  // open: Qn, preset, reset
  and and_49 (and_49_out, and_1_out, not_13_out, d_ff_22_q);
  D_Flip_Flop #(.trigger("high")) d_ff_28 (.D(and_49_out), .clk(and_9_out), .Q(d_ff_28_q));  // open: Qn, preset, reset
  and and_50 (and_50_out, and_2_out, not_13_out, d_ff_22_q);
  D_Flip_Flop #(.trigger("high")) d_ff_29 (.D(and_50_out), .clk(and_10_out), .Q(d_ff_29_q));  // open: Qn, preset, reset
  and and_51 (and_51_out, and_3_out, not_13_out, d_ff_22_q);
  D_Flip_Flop #(.trigger("high")) d_ff_30 (.D(and_51_out), .clk(and_11_out), .Q(d_ff_30_q));  // open: Qn, preset, reset
  and and_52 (and_52_out, and_4_out, not_13_out, d_ff_22_q);
  D_Flip_Flop #(.trigger("high")) d_ff_31 (.D(and_52_out), .clk(and_12_out), .Q(d_ff_31_q));  // open: Qn, preset, reset
  and and_53 (and_53_out, and_5_out, not_13_out, d_ff_22_q);
  D_Flip_Flop #(.trigger("high")) d_ff_32 (.D(and_53_out), .clk(and_13_out), .Q(d_ff_32_q));  // open: Qn, preset, reset
  and and_54 (and_54_out, and_6_out, not_13_out, d_ff_22_q);
  D_Flip_Flop #(.trigger("high")) d_ff_33 (.D(and_54_out), .clk(and_14_out), .Q(d_ff_33_q));  // open: Qn, preset, reset
  and and_55 (and_55_out, and_7_out, not_13_out, d_ff_22_q);
  D_Flip_Flop #(.trigger("high")) d_ff_34 (.D(and_55_out), .clk(and_15_out), .Q(d_ff_34_q));  // open: Qn, preset, reset
  and and_56 (and_56_out, and_8_out, not_13_out, d_ff_22_q);
  D_Flip_Flop #(.trigger("high")) d_ff_35 (.D(and_56_out), .clk(and_16_out), .Q(X1));  // open: Qn, preset, reset
  or or_3 (or_3_out, and_57_out, and_58_out, and_59_out, and_60_out, and_61_out, and_62_out, and_63_out, and_64_out);
  and and_57 (and_57_out, d_ff_28_q, and_1_out, mode);
  and and_58 (and_58_out, d_ff_29_q, and_2_out, mode);
  and and_59 (and_59_out, d_ff_30_q, and_3_out, mode);
  and and_60 (and_60_out, d_ff_31_q, and_4_out, mode);
  and and_61 (and_61_out, d_ff_32_q, and_5_out, mode);
  and and_62 (and_62_out, d_ff_33_q, and_6_out, mode);
  and and_63 (and_63_out, d_ff_34_q, and_7_out, mode);
  and and_64 (and_64_out, X1, and_8_out, mode);
  and and_65 (DRo3, d_ff_23_q, mode);
  and and_66 (and_66_out, and_1_out, not_13_out, d_ff_24_q);
  D_Flip_Flop #(.trigger("high")) d_ff_36 (.D(and_66_out), .clk(and_9_out), .Q(d_ff_36_q));  // open: Qn, preset, reset
  and and_67 (and_67_out, and_2_out, not_13_out, d_ff_24_q);
  D_Flip_Flop #(.trigger("high")) d_ff_37 (.D(and_67_out), .clk(and_10_out), .Q(d_ff_37_q));  // open: Qn, preset, reset
  and and_68 (and_68_out, and_3_out, not_13_out, d_ff_24_q);
  D_Flip_Flop #(.trigger("high")) d_ff_38 (.D(and_68_out), .clk(and_11_out), .Q(d_ff_38_q));  // open: Qn, preset, reset
  and and_69 (and_69_out, and_4_out, not_13_out, d_ff_24_q);
  D_Flip_Flop #(.trigger("high")) d_ff_39 (.D(and_69_out), .clk(and_12_out), .Q(d_ff_39_q));  // open: Qn, preset, reset
  and and_70 (and_70_out, and_5_out, not_13_out, d_ff_24_q);
  D_Flip_Flop #(.trigger("high")) d_ff_40 (.D(and_70_out), .clk(and_13_out), .Q(d_ff_40_q));  // open: Qn, preset, reset
  and and_71 (and_71_out, and_6_out, not_13_out, d_ff_24_q);
  D_Flip_Flop #(.trigger("high")) d_ff_41 (.D(and_71_out), .clk(and_14_out), .Q(d_ff_41_q));  // open: Qn, preset, reset
  and and_72 (and_72_out, and_7_out, not_13_out, d_ff_24_q);
  D_Flip_Flop #(.trigger("high")) d_ff_42 (.D(and_72_out), .clk(and_15_out), .Q(d_ff_42_q));  // open: Qn, preset, reset
  and and_73 (and_73_out, and_8_out, not_13_out, d_ff_24_q);
  D_Flip_Flop #(.trigger("high")) d_ff_43 (.D(and_73_out), .clk(and_16_out), .Q(X0));  // open: Qn, preset, reset
  and and_74 (DRo2, d_ff_25_q, mode);
  or or_4 (or_4_out, and_75_out, and_76_out, and_77_out, and_78_out, and_79_out, and_80_out, and_81_out, and_82_out);
  and and_75 (and_75_out, d_ff_36_q, and_1_out, mode);
  and and_76 (and_76_out, d_ff_37_q, and_2_out, mode);
  and and_77 (and_77_out, d_ff_38_q, and_3_out, mode);
  and and_78 (and_78_out, d_ff_39_q, and_4_out, mode);
  and and_79 (and_79_out, d_ff_40_q, and_5_out, mode);
  and and_80 (and_80_out, d_ff_41_q, and_6_out, mode);
  and and_81 (and_81_out, d_ff_42_q, and_7_out, mode);
  and and_82 (and_82_out, X0, and_8_out, mode);
  and and_83 (DRo1, d_ff_26_q, mode);
  and and_84 (DRo0, d_ff_27_q, mode);

  // Other names for the same wires on the sheet: RAMmode = mode

  // Notes on the sheet:
  //   3-bit address input pins
  //   Mode input pin
  //   4-bit data input pins
  //   4-bit data output pins
endmodule

module R0 (
  input  d3,
  input  d2,
  input  d1,
  input  d0,
  input  o,
  input  clk,
  input  i,
  output b3,
  output b2,
  output b1,
  output b0
);

  wire and_1_out, d_ff_1_q, d_ff_2_q, d_ff_3_q, d_ff_4_q, not_1_out;

  not not_1 (not_1_out, clk);
  and and_1 (and_1_out, not_1_out, i);
  D_Flip_Flop d_ff_1 (.D(d0), .clk(and_1_out), .Q(d_ff_1_q));  // open: Qn, preset, reset
  D_Flip_Flop d_ff_2 (.D(d1), .clk(and_1_out), .Q(d_ff_2_q));  // open: Qn, preset, reset
  D_Flip_Flop d_ff_3 (.D(d2), .clk(and_1_out), .Q(d_ff_3_q));  // open: Qn, preset, reset
  D_Flip_Flop d_ff_4 (.D(d3), .clk(and_1_out), .Q(d_ff_4_q));  // open: Qn, preset, reset
  and and_2 (b0, o, d_ff_1_q);
  and and_3 (b1, o, d_ff_2_q);
  and and_4 (b2, o, d_ff_3_q);
  and and_5 (b3, o, d_ff_4_q);

  // Notes on the sheet:
  //   Input
  //   1 = write
  //   0 = read
  //   Output
endmodule

module R1 (
  input  d3,
  input  d2,
  input  d1,
  input  d0,
  input  o,
  input  clk,
  input  i,
  output b3,
  output b2,
  output b1,
  output b0
);

  wire and_1_out, d_ff_1_q, d_ff_2_q, d_ff_3_q, d_ff_4_q, not_1_out;

  not not_1 (not_1_out, clk);
  and and_1 (and_1_out, not_1_out, i);
  D_Flip_Flop d_ff_1 (.D(d0), .clk(and_1_out), .Q(d_ff_1_q));  // open: Qn, preset, reset
  D_Flip_Flop d_ff_2 (.D(d1), .clk(and_1_out), .Q(d_ff_2_q));  // open: Qn, preset, reset
  D_Flip_Flop d_ff_3 (.D(d2), .clk(and_1_out), .Q(d_ff_3_q));  // open: Qn, preset, reset
  D_Flip_Flop d_ff_4 (.D(d3), .clk(and_1_out), .Q(d_ff_4_q));  // open: Qn, preset, reset
  and and_2 (b0, o, d_ff_1_q);
  and and_3 (b1, o, d_ff_2_q);
  and and_4 (b2, o, d_ff_3_q);
  and and_5 (b3, o, d_ff_4_q);

  // Notes on the sheet:
  //   Input
  //   1 = write
  //   0 = read
  //   Output
endmodule

module MAR (
  input  d2,
  input  d1,
  input  d0,
  input  o,
  input  clk,
  input  i,
  output b2,
  output b1,
  output b0
);

  wire and_1_out, d_ff_1_q, d_ff_2_q, d_ff_3_q, not_1_out;

  not not_1 (not_1_out, clk);
  and and_1 (and_1_out, not_1_out, i);
  D_Flip_Flop d_ff_1 (.D(d0), .clk(and_1_out), .Q(d_ff_1_q));  // open: Qn, preset, reset
  D_Flip_Flop d_ff_2 (.D(d1), .clk(and_1_out), .Q(d_ff_2_q));  // open: Qn, preset, reset
  D_Flip_Flop d_ff_3 (.D(d2), .clk(and_1_out), .Q(d_ff_3_q));  // open: Qn, preset, reset
  and and_2 (b0, o, d_ff_1_q);
  and and_3 (b1, o, d_ff_2_q);
  and and_4 (b2, o, d_ff_3_q);

  // Notes on the sheet:
  //   Input
  //   1 = write
  //   0 = read
  //   Output
endmodule

module MBR (
  input  d3,
  input  d2,
  input  d1,
  input  d0,
  input  o,
  input  clk,
  input  i,
  output b3,
  output b2,
  output b1,
  output b0
);

  wire and_1_out, d_ff_1_q, d_ff_2_q, d_ff_3_q, d_ff_4_q, not_1_out;

  not not_1 (not_1_out, clk);
  and and_1 (and_1_out, not_1_out, i);
  D_Flip_Flop d_ff_1 (.D(d0), .clk(and_1_out), .Q(d_ff_1_q));  // open: Qn, preset, reset
  D_Flip_Flop d_ff_2 (.D(d1), .clk(and_1_out), .Q(d_ff_2_q));  // open: Qn, preset, reset
  D_Flip_Flop d_ff_3 (.D(d2), .clk(and_1_out), .Q(d_ff_3_q));  // open: Qn, preset, reset
  D_Flip_Flop d_ff_4 (.D(d3), .clk(and_1_out), .Q(d_ff_4_q));  // open: Qn, preset, reset
  and and_2 (b0, o, d_ff_1_q);
  and and_3 (b1, o, d_ff_2_q);
  and and_4 (b2, o, d_ff_3_q);
  and and_5 (b3, o, d_ff_4_q);

  // Notes on the sheet:
  //   Input
  //   1 = write
  //   0 = read
  //   Output
endmodule

module CU (
  input  ir3,
  input  ir2,
  input  ir1,
  input  ir0,
  input  clk,
  output HALT,
  output PCi,
  output PCo,
  output RAMmode,
  output RAMrun,
  output MARi,
  output MARo,
  output MBRi,
  output MBRo,
  output IRi,
  output IRo,
  output R0i,
  output R0o,
  output R1i,
  output R1o,
  output Li,
  output Ri,
  output ALUop,
  output ALUrun,
  output AOUTo,
  output CUadr
);

  wire add_out, and_1_out, and_2_out, and_3_out, and_4_out, and_5_out, and_7_out, and_9_out, and_10_out,
       and_12_out, and_13_out, and_14_out, and_15_out, and_16_out, and_17_out, and_18_out, and_19_out,
       and_20_out, and_21_out, and_22_out, and_23_out, and_24_out, and_25_out, and_26_out, and_27_out,
       and_28_out, and_29_out, and_30_out, and_31_out, and_32_out, and_33_out, incrementor_1_pc0,
       incrementor_1_pc1, incrementor_1_pc2, load_out, not_1_out, not_2_out, not_3_out, not_4_out, not_5_out,
       not_6_out, not_7_out, not_8_out, not_9_out, not_10_out, not_11_out, not_12_out, not_13_out,
       not_14_out, not_15_out, not_16_out, not_17_out, not_18_out, not_19_out, not_20_out, not_21_out,
       not_22_out, not_23_out, not_24_out, not_25_out, not_26_out, not_27_out, not_28_out, not_29_out,
       not_30_out, not_31_out, not_32_out, not_33_out, not_34_out, S0, S1, save_out, sub_out;

  not not_1 (not_1_out, ir3);
  not not_2 (not_2_out, ir2);
  not not_3 (not_3_out, ir3);
  and load (load_out, not_1_out, not_2_out);
  and save (save_out, not_3_out, ir2);
  and add (add_out, ir3, not_4_out);
  not not_4 (not_4_out, ir2);
  and sub (sub_out, ir3, ir2);
  and and_1 (and_1_out, ir3, ir2, ir1, ir0);
  not not_5 (not_5_out, and_1_out);
  and and_2 (and_2_out, ir3, ir2, ir1, ir0);
  and and_3 (and_3_out, sub_out, not_5_out);
  not not_6 (not_6_out, IRo);
  not not_7 (not_7_out, S1);
  not not_8 (not_8_out, S0);
  not not_9 (not_9_out, IRo);
  not not_10 (not_10_out, S1);
  not not_11 (not_11_out, IRo);
  not not_12 (not_12_out, S0);
  not not_13 (not_13_out, IRo);
  not not_14 (not_14_out, S1);
  not not_15 (not_15_out, S0);
  not not_16 (not_16_out, S1);
  not not_17 (not_17_out, S0);
  not not_18 (not_18_out, S1);
  not not_19 (not_19_out, S0);
  not not_20 (not_20_out, S1);
  not not_21 (not_21_out, S0);
  not not_22 (not_22_out, S1);
  not not_23 (not_23_out, S0);
  not not_24 (not_24_out, S1);
  not not_25 (not_25_out, S0);
  not not_26 (not_26_out, S1);
  and and_4 (and_4_out, IRo, not_26_out, not_27_out, and_3_out);
  not not_27 (not_27_out, S0);
  not not_28 (not_28_out, S1);
  and and_5 (and_5_out, IRo, not_28_out, S0, and_3_out);
  and and_6 (ALUop, IRo, S1, not_29_out, and_3_out);
  not not_29 (not_29_out, S0);
  and and_7 (and_7_out, IRo, S1, S0, and_3_out);
  D_Flip_Flop d_ff_1 (.D(and_2_out), .clk(not_30_out), .Q(HALT));  // open: Qn, preset, reset
  not not_30 (not_30_out, clk);
  and and_8 (PCi, not_6_out, not_7_out, not_8_out, clk);
  and and_9 (and_9_out, not_9_out, not_10_out, S0);
  and and_10 (and_10_out, not_11_out, S1, not_12_out);
  and and_11 (IRi, not_13_out, S1, S0);
  and and_12 (and_12_out, IRo, not_14_out, not_15_out, load_out);
  and and_13 (and_13_out, IRo, not_16_out, S0, load_out);
  and and_14 (and_14_out, IRo, S1, not_17_out, load_out);
  and and_15 (and_15_out, IRo, S1, S0, load_out);
  and and_16 (and_16_out, IRo, not_18_out, not_19_out, save_out);
  and and_17 (and_17_out, IRo, not_20_out, S0, save_out);
  and and_18 (and_18_out, IRo, S1, not_21_out, save_out);
  and and_19 (and_19_out, IRo, S1, S0, save_out);
  and and_20 (and_20_out, IRo, not_22_out, not_23_out, add_out);
  and and_21 (and_21_out, IRo, not_24_out, S0, add_out);
  and and_22 (and_22_out, IRo, S1, not_25_out, add_out);
  and and_23 (and_23_out, IRo, S1, S0, add_out);
  incrementor incrementor_1 (
    .b2(IRo), .b1(S1), .b0(S0), .pc2(incrementor_1_pc2), .pc1(incrementor_1_pc1), .pc0(incrementor_1_pc0));
  Microstep microstep_1 (
    .d2(incrementor_1_pc2), .d1(incrementor_1_pc1), .d0(incrementor_1_pc0), .o(1'b1), .clk(clk), .i(1'b1),
    .b2(IRo), .b1(S1), .b0(S0));
  not not_31 (not_31_out, ir1);
  and and_24 (and_24_out, not_31_out, and_15_out);
  not not_32 (not_32_out, ir1);
  and and_25 (and_25_out, not_32_out, and_21_out);
  and and_26 (and_26_out, ir1, and_21_out);
  or or_1 (RAMmode, and_9_out, and_10_out, and_13_out, and_14_out);
  or or_2 (RAMrun, and_9_out, and_10_out, and_13_out, and_14_out, and_18_out, and_19_out);
  or or_3 (MARi, PCi, and_16_out, and_12_out);
  or or_4 (MARo, and_9_out, and_10_out, and_13_out, and_14_out, and_18_out, and_19_out);
  or or_5 (MBRi, and_10_out, and_14_out, and_17_out);
  or or_6 (MBRo, IRi, and_15_out, and_18_out, and_19_out);
  or or_7 (R0i, and_24_out, and_23_out, and_7_out);
  not not_33 (not_33_out, ir1);
  and and_27 (and_27_out, not_33_out, and_17_out);
  not not_34 (not_34_out, ir1);
  and and_28 (and_28_out, not_34_out, and_5_out);
  and and_29 (and_29_out, ir1, and_15_out);
  buf or_8 (R1i, and_29_out);  // OR_Gate
  and and_30 (and_30_out, ir1, and_17_out);
  or or_9 (R1o, and_30_out, and_26_out, and_31_out);
  and and_31 (and_31_out, ir1, and_5_out);
  and and_32 (and_32_out, ir0, and_12_out);
  or or_10 (CUadr, and_32_out, and_33_out);
  and and_33 (and_33_out, ir0, and_16_out);
  or or_11 (R0o, and_27_out, and_20_out, and_25_out, and_4_out, and_28_out);
  or or_12 (Li, and_20_out, and_4_out);
  or or_13 (Ri, and_21_out, and_5_out);
  or or_14 (ALUrun, and_22_out, ALUop);
  or or_15 (AOUTo, and_23_out, and_7_out);

  assign PCo = PCi;

  // Other names for the same wires on the sheet: S2 = IRo

  // Notes on the sheet:
  //   microstep greater or equal to 4: output IR everytime
  //   PC-MAR
  //   RAM(AR)-MBR
  //   MBR-IR
  //   R0-L
  //   Aout-R0
  //   R0-L
  //   R0/R1-R
  //   ALU execution
  //   Aout-R0
  //   MAR-AR 1-mode
  //   address 0/1 - MAR
  //   MAR-AR  mode1-mode
  //   RAM(ar)-MBR
  //   MBR-R0/R1
  //   address 0/1 - MAR
  //   R0/R1-MBR
  //   MAR-AR  0-mode  MBR-DR
  //   DR-RAM(AR)
  //   R0/R1-R
  //   ALU execution
endmodule

module PC (
  input  d2,
  input  d1,
  input  d0,
  input  o,
  input  clk,
  input  i,
  output b2,
  output b1,
  output b0
);

  wire and_1_out, d_ff_1_q, d_ff_2_q, d_ff_3_q, not_1_out;

  not not_1 (not_1_out, clk);
  and and_1 (and_1_out, not_1_out, i);
  D_Flip_Flop d_ff_1 (.D(d0), .clk(and_1_out), .Q(d_ff_1_q));  // open: Qn, preset, reset
  D_Flip_Flop d_ff_2 (.D(d1), .clk(and_1_out), .Q(d_ff_2_q));  // open: Qn, preset, reset
  D_Flip_Flop d_ff_3 (.D(d2), .clk(and_1_out), .Q(d_ff_3_q));  // open: Qn, preset, reset
  and and_2 (b0, o, d_ff_1_q);
  and and_3 (b1, o, d_ff_2_q);
  and and_4 (b2, o, d_ff_3_q);

  // Notes on the sheet:
  //   Input
  //   1 = write
  //   0 = read
  //   Output
endmodule

module ALU (
  input  L3,
  input  L2,
  input  L1,
  input  L0,
  input  R3,
  input  R2,
  input  R1,
  input  R0,
  input  clk,
  input  AddSub,
  output signed_overflow,
  output overflow,
  output zero,
  output negative,
  output Aout3,
  output Aout2,
  output Aout1,
  output Aout0
);

  wire and_1_out, and_2_out, and_3_out, and_4_out, and_5_out, and_6_out, and_7_out, and_8_out, and_9_out,
       and_10_out, and_11_out, and_12_out, and_13_out, and_14_out, and_15_out, and_16_out, and_17_out,
       and_18_out, and_19_out, and_20_out, and_23_out, and_24_out, and_26_out, and_27_out, and_28_out,
       and_29_out, and_30_out, and_31_out, and_32_out, and_33_out, not_1_out, not_2_out, not_3_out,
       not_4_out, not_5_out, not_6_out, not_7_out, not_8_out, not_9_out, not_10_out, not_11_out, not_12_out,
       not_13_out, or_1_out, or_3_out, or_5_out, or_7_out, or_8_out, or_9_out, or_11_out, xor_1_out,
       xor_2_out, xor_3_out, xor_5_out, xor_6_out, xor_7_out, xor_8_out;

  not not_1 (not_1_out, AddSub);
  and and_1 (and_1_out, or_7_out, and_10_out);
  and and_2 (and_2_out, and_10_out, or_3_out);
  or or_1 (or_1_out, and_1_out, and_2_out, and_3_out);
  and and_3 (and_3_out, or_7_out, or_3_out);
  ExactlyOne xor_1 (.out(xor_1_out), .in0(and_10_out), .in1(or_7_out), .in2(or_3_out));
  and and_4 (and_4_out, and_12_out, or_8_out);
  and and_5 (and_5_out, and_10_out, or_7_out, or_3_out);
  or or_2 (Aout3, xor_1_out, and_5_out);
  and and_6 (and_6_out, and_12_out, or_5_out);
  and and_7 (and_7_out, or_8_out, or_5_out);
  or or_3 (or_3_out, and_4_out, and_6_out, and_7_out);
  ExactlyOne xor_2 (.out(xor_2_out), .in0(and_12_out), .in1(or_8_out), .in2(or_5_out));
  and and_8 (and_8_out, and_14_out, or_9_out);
  and and_9 (and_9_out, and_12_out, or_8_out, or_5_out);
  or or_4 (Aout2, xor_2_out, and_9_out);
  and and_10 (and_10_out, L3, clk);
  and and_11 (and_11_out, and_14_out, and_15_out);
  or or_5 (or_5_out, and_8_out, and_11_out, and_13_out);
  and and_12 (and_12_out, L2, clk);
  and and_13 (and_13_out, or_9_out, and_15_out);
  ExactlyOne xor_3 (.out(xor_3_out), .in0(and_14_out), .in1(or_9_out), .in2(and_15_out));
  and and_14 (and_14_out, L1, clk);
  and and_15 (and_15_out, and_17_out, or_11_out);
  and and_16 (and_16_out, and_14_out, or_9_out, and_15_out);
  or or_6 (Aout1, xor_3_out, and_16_out);
  and and_17 (and_17_out, L0, clk);
  xor xor_4 (Aout0, and_17_out, or_11_out);
  and and_18 (and_18_out, clk, AddSub, R3);
  not not_2 (not_2_out, and_18_out);
  and and_19 (and_19_out, not_3_out, and_24_out);
  xor xor_5 (xor_5_out, not_2_out, and_19_out);
  or or_7 (or_7_out, xor_5_out, and_30_out);
  and and_20 (and_20_out, clk, AddSub, R2);
  not not_3 (not_3_out, and_20_out);
  xor xor_6 (xor_6_out, not_3_out, and_24_out);
  and and_21 (negative, Aout3, clk);
  not not_4 (not_4_out, Aout3);
  not not_5 (not_5_out, Aout2);
  and and_22 (zero, not_4_out, not_5_out, clk, not_6_out, not_7_out);
  not not_6 (not_6_out, Aout1);
  not not_7 (not_7_out, Aout0);
  not not_8 (not_8_out, Aout3);
  not not_9 (not_9_out, and_10_out);
  not not_10 (not_10_out, or_7_out);
  and and_23 (and_23_out, clk, AddSub, R1);
  not not_11 (not_11_out, and_23_out);
  and and_24 (and_24_out, not_11_out, and_28_out);
  or or_8 (or_8_out, xor_6_out, and_31_out);
  and and_25 (overflow, clk, not_1_out, or_1_out);
  and and_26 (and_26_out, and_10_out, or_7_out, not_8_out);
  and and_27 (and_27_out, not_9_out, not_10_out, Aout3);
  and and_28 (and_28_out, not_12_out, 1'b1);
  xor xor_7 (xor_7_out, not_11_out, and_28_out);
  or or_9 (or_9_out, xor_7_out, and_32_out);
  or or_10 (signed_overflow, and_26_out, and_27_out);
  and and_29 (and_29_out, clk, AddSub, R0);
  not not_12 (not_12_out, and_29_out);
  xor xor_8 (xor_8_out, not_12_out, 1'b1);
  or or_11 (or_11_out, xor_8_out, and_33_out);
  not not_13 (not_13_out, AddSub);
  and and_30 (and_30_out, not_13_out, clk, R3);
  and and_31 (and_31_out, not_13_out, clk, R2);
  and and_32 (and_32_out, not_13_out, clk, R1);
  and and_33 (and_33_out, not_13_out, clk, R0);

  // Notes on the sheet:
  //   An Ni Xu 261053392
  //   Add/Sub command
  //   A-out output
  //   L input
  //   R input
  //   Status Determination
  //   2's complement
endmodule

module D (
  input  d3,
  input  d2,
  input  d1,
  input  d0,
  input  clk,
  output l_b,
  output l_c,
  output a,
  output b,
  output c,
  output dd,
  output e,
  output f,
  output g
);

  wire and_1_out, and_2_out, and_3_out, and_4_out, and_5_out, and_6_out, and_7_out, and_8_out, and_9_out,
       and_10_out, and_11_out, and_12_out, and_13_out, and_16_out, and_17_out, and_18_out, and_19_out,
       and_20_out, and_21_out, and_22_out, and_23_out, and_24_out, and_25_out, and_26_out, and_27_out,
       and_28_out, and_29_out, and_30_out, d_ff_1_q, d_ff_2_q, d_ff_3_q, d_ff_4_q, not_1_out, not_2_out,
       not_3_out, not_4_out, not_5_out, or_1_out, or_2_out, or_3_out, xor_1_out, xor_2_out, xor_3_out,
       xor_4_out;

  D_Flip_Flop d_ff_1 (.D(d0), .clk(clk), .Q(d_ff_1_q));  // open: Qn, preset, reset
  D_Flip_Flop d_ff_2 (.D(d1), .clk(clk), .Q(d_ff_2_q));  // open: Qn, preset, reset
  D_Flip_Flop d_ff_3 (.D(d2), .clk(clk), .Q(d_ff_3_q));  // open: Qn, preset, reset
  D_Flip_Flop d_ff_4 (.D(d3), .clk(clk), .Q(d_ff_4_q));  // open: Qn, preset, reset
  not not_1 (not_1_out, d_ff_1_q);
  not not_2 (not_2_out, d_ff_2_q);
  not not_3 (not_3_out, d_ff_3_q);
  not not_4 (not_4_out, d_ff_4_q);
  or or_1 (or_1_out, d_ff_3_q, d_ff_2_q);
  or or_2 (or_2_out, d_ff_3_q, d_ff_2_q);
  and and_1 (and_1_out, d_ff_1_q, d_ff_3_q);
  and and_2 (and_2_out, not_1_out, not_3_out);
  and and_3 (and_3_out, d_ff_2_q, not_4_out);
  and and_4 (and_4_out, not_2_out, d_ff_4_q);
  and and_5 (and_5_out, not_2_out, not_1_out);
  xor xor_1 (xor_1_out, d_ff_2_q, d_ff_1_q);
  xor xor_2 (xor_2_out, d_ff_4_q, d_ff_2_q);
  xor xor_3 (xor_3_out, d_ff_4_q, d_ff_3_q);
  and and_6 (and_6_out, not_3_out, not_1_out);
  and and_7 (and_7_out, not_4_out, not_3_out, d_ff_2_q);
  and and_8 (and_8_out, d_ff_4_q, d_ff_3_q, d_ff_1_q);
  and and_9 (and_9_out, not_4_out, not_1_out, d_ff_2_q);
  and and_10 (and_10_out, d_ff_3_q, d_ff_1_q, not_2_out);
  and and_11 (and_11_out, not_2_out, d_ff_4_q);
  or or_3 (or_3_out, not_4_out, d_ff_4_q);
  and and_12 (and_12_out, d_ff_3_q, not_2_out);
  and and_13 (and_13_out, not_3_out, d_ff_2_q);
  and and_14 (l_b, d_ff_4_q, or_1_out);
  and and_15 (l_c, d_ff_4_q, or_2_out);
  or or_4 (a, and_1_out, and_2_out, and_3_out, and_4_out);
  and and_16 (and_16_out, d_ff_4_q, xor_1_out);
  and and_17 (and_17_out, not_4_out, d_ff_3_q, d_ff_2_q, d_ff_1_q);
  not not_5 (not_5_out, xor_2_out);
  and and_18 (and_18_out, or_3_out, not_3_out, not_1_out);
  and and_19 (and_19_out, not_4_out, d_ff_3_q, d_ff_2_q, not_1_out);
  and and_20 (and_20_out, not_2_out, not_1_out, d_ff_4_q, d_ff_3_q);
  and and_21 (and_21_out, not_3_out, not_2_out, not_1_out);
  and and_22 (and_22_out, not_4_out, not_2_out, d_ff_3_q);
  and and_23 (and_23_out, not_3_out, not_2_out, d_ff_4_q);
  and and_24 (and_24_out, d_ff_4_q, d_ff_3_q, d_ff_2_q);
  and and_25 (and_25_out, not_3_out, not_1_out, d_ff_4_q, d_ff_2_q);
  and and_26 (and_26_out, not_4_out, not_1_out, d_ff_3_q, d_ff_2_q);
  and and_27 (and_27_out, d_ff_4_q, d_ff_3_q);
  and and_28 (and_28_out, not_2_out, d_ff_4_q);
  xor xor_4 (xor_4_out, and_12_out, and_13_out);
  and and_29 (and_29_out, not_4_out, not_1_out, d_ff_3_q);
  or or_5 (b, not_3_out, and_5_out, and_16_out, and_17_out);
  or or_6 (c, d_ff_1_q, not_5_out, xor_3_out);
  or or_7 (dd, and_6_out, and_7_out, and_8_out, and_9_out, and_10_out, and_11_out);
  or or_8 (e, and_18_out, and_19_out, and_20_out);
  and and_30 (and_30_out, not_4_out, xor_4_out);
  or or_9 (f, and_21_out, and_22_out, and_23_out, and_24_out, and_25_out, and_26_out);
  or or_10 (g, and_27_out, and_28_out, and_30_out, and_29_out);

  // Notes on the sheet:
  //   Input
  //   Output
endmodule

module incrementor (
  input  b2,
  input  b1,
  input  b0,
  output pc2,
  output pc1,
  output pc0
);

  wire and_1_out, and_2_out;

  and and_1 (and_1_out, b1, and_2_out);
  xor xor_1 (pc2, b2, and_1_out);
  and and_2 (and_2_out, b0, 1'b1);
  xor xor_2 (pc1, b1, and_2_out);
  xor xor_3 (pc0, b0, 1'b1);
endmodule

module IR (
  input  d3,
  input  d2,
  input  d1,
  input  d0,
  input  o,
  input  clk,
  input  i,
  output b3,
  output b2,
  output b1,
  output b0
);

  wire and_1_out, d_ff_1_q, d_ff_2_q, d_ff_3_q, d_ff_4_q, not_1_out;

  not not_1 (not_1_out, clk);
  and and_1 (and_1_out, not_1_out, i);
  D_Flip_Flop d_ff_1 (.D(d0), .clk(and_1_out), .Q(d_ff_1_q));  // open: Qn, preset, reset
  D_Flip_Flop d_ff_2 (.D(d1), .clk(and_1_out), .Q(d_ff_2_q));  // open: Qn, preset, reset
  D_Flip_Flop d_ff_3 (.D(d2), .clk(and_1_out), .Q(d_ff_3_q));  // open: Qn, preset, reset
  D_Flip_Flop d_ff_4 (.D(d3), .clk(and_1_out), .Q(d_ff_4_q));  // open: Qn, preset, reset
  and and_2 (b0, o, d_ff_1_q);
  and and_3 (b1, o, d_ff_2_q);
  and and_4 (b2, o, d_ff_3_q);
  and and_5 (b3, o, d_ff_4_q);

  // Notes on the sheet:
  //   Input
  //   1 = write
  //   0 = read
  //   Output
endmodule

module L (
  input  d3,
  input  d2,
  input  d1,
  input  d0,
  input  o,
  input  clk,
  input  i,
  output b3,
  output b2,
  output b1,
  output b0
);

  wire and_1_out, d_ff_1_q, d_ff_2_q, d_ff_3_q, d_ff_4_q, not_1_out;

  not not_1 (not_1_out, clk);
  and and_1 (and_1_out, not_1_out, i);
  D_Flip_Flop d_ff_1 (.D(d0), .clk(and_1_out), .Q(d_ff_1_q));  // open: Qn, preset, reset
  D_Flip_Flop d_ff_2 (.D(d1), .clk(and_1_out), .Q(d_ff_2_q));  // open: Qn, preset, reset
  D_Flip_Flop d_ff_3 (.D(d2), .clk(and_1_out), .Q(d_ff_3_q));  // open: Qn, preset, reset
  D_Flip_Flop d_ff_4 (.D(d3), .clk(and_1_out), .Q(d_ff_4_q));  // open: Qn, preset, reset
  and and_2 (b0, o, d_ff_1_q);
  and and_3 (b1, o, d_ff_2_q);
  and and_4 (b2, o, d_ff_3_q);
  and and_5 (b3, o, d_ff_4_q);

  // Notes on the sheet:
  //   Input
  //   1 = write
  //   0 = read
  //   Output
endmodule

module R (
  input  d3,
  input  d2,
  input  d1,
  input  d0,
  input  o,
  input  clk,
  input  i,
  output b3,
  output b2,
  output b1,
  output b0
);

  wire and_1_out, d_ff_1_q, d_ff_2_q, d_ff_3_q, d_ff_4_q, not_1_out;

  not not_1 (not_1_out, clk);
  and and_1 (and_1_out, not_1_out, i);
  D_Flip_Flop d_ff_1 (.D(d0), .clk(and_1_out), .Q(d_ff_1_q));  // open: Qn, preset, reset
  D_Flip_Flop d_ff_2 (.D(d1), .clk(and_1_out), .Q(d_ff_2_q));  // open: Qn, preset, reset
  D_Flip_Flop d_ff_3 (.D(d2), .clk(and_1_out), .Q(d_ff_3_q));  // open: Qn, preset, reset
  D_Flip_Flop d_ff_4 (.D(d3), .clk(and_1_out), .Q(d_ff_4_q));  // open: Qn, preset, reset
  and and_2 (b0, o, d_ff_1_q);
  and and_3 (b1, o, d_ff_2_q);
  and and_4 (b2, o, d_ff_3_q);
  and and_5 (b3, o, d_ff_4_q);

  // Notes on the sheet:
  //   Input
  //   1 = write
  //   0 = read
  //   Output
endmodule

module Aout (
  input  d3,
  input  d2,
  input  d1,
  input  d0,
  input  o,
  input  clk,
  input  i,
  output b3,
  output b2,
  output b1,
  output b0
);

  wire and_1_out, d_ff_1_q, d_ff_2_q, d_ff_3_q, d_ff_4_q, not_1_out;

  not not_1 (not_1_out, clk);
  and and_1 (and_1_out, not_1_out, i);
  D_Flip_Flop d_ff_1 (.D(d0), .clk(and_1_out), .Q(d_ff_1_q));  // open: Qn, preset, reset
  D_Flip_Flop d_ff_2 (.D(d1), .clk(and_1_out), .Q(d_ff_2_q));  // open: Qn, preset, reset
  D_Flip_Flop d_ff_3 (.D(d2), .clk(and_1_out), .Q(d_ff_3_q));  // open: Qn, preset, reset
  D_Flip_Flop d_ff_4 (.D(d3), .clk(and_1_out), .Q(d_ff_4_q));  // open: Qn, preset, reset
  and and_2 (b0, o, d_ff_1_q);
  and and_3 (b1, o, d_ff_2_q);
  and and_4 (b2, o, d_ff_3_q);
  and and_5 (b3, o, d_ff_4_q);

  // Notes on the sheet:
  //   Input
  //   1 = write
  //   0 = read
  //   Output
endmodule

module Status (
  input  d3,
  input  d2,
  input  d1,
  input  d0,
  input  o,
  input  clk,
  input  i,
  output b3,
  output b2,
  output b1,
  output b0
);

  wire and_1_out, d_ff_1_q, d_ff_2_q, d_ff_3_q, d_ff_4_q, not_1_out;

  not not_1 (not_1_out, clk);
  and and_1 (and_1_out, not_1_out, i);
  D_Flip_Flop d_ff_1 (.D(d0), .clk(and_1_out), .Q(d_ff_1_q));  // open: Qn, preset, reset
  D_Flip_Flop d_ff_2 (.D(d1), .clk(and_1_out), .Q(d_ff_2_q));  // open: Qn, preset, reset
  D_Flip_Flop d_ff_3 (.D(d2), .clk(and_1_out), .Q(d_ff_3_q));  // open: Qn, preset, reset
  D_Flip_Flop d_ff_4 (.D(d3), .clk(and_1_out), .Q(d_ff_4_q));  // open: Qn, preset, reset
  and and_2 (b0, o, d_ff_1_q);
  and and_3 (b1, o, d_ff_2_q);
  and and_4 (b2, o, d_ff_3_q);
  and and_5 (b3, o, d_ff_4_q);

  // Notes on the sheet:
  //   Input
  //   1 = write
  //   0 = read
  //   Output
endmodule

module PCincrementor (
  input  b2,
  input  b1,
  input  b0,
  output pc2,
  output pc1,
  output pc0
);

  wire and_1_out, and_2_out;

  and and_1 (and_1_out, b1, and_2_out);
  xor xor_1 (pc2, b2, and_1_out);
  and and_2 (and_2_out, b0, 1'b1);
  xor xor_2 (pc1, b1, and_2_out);
  xor xor_3 (pc0, b0, 1'b1);
endmodule

module Microstep (
  input  d2,
  input  d1,
  input  d0,
  input  o,
  input  clk,
  input  i,
  output b2,
  output b1,
  output b0
);

  wire and_1_out, d_ff_1_q, d_ff_2_q, d_ff_3_q, not_1_out;

  not not_1 (not_1_out, clk);
  and and_1 (and_1_out, not_1_out, i);
  D_Flip_Flop d_ff_1 (.D(d0), .clk(and_1_out), .Q(d_ff_1_q));  // open: Qn, preset, reset
  D_Flip_Flop d_ff_2 (.D(d1), .clk(and_1_out), .Q(d_ff_2_q));  // open: Qn, preset, reset
  D_Flip_Flop d_ff_3 (.D(d2), .clk(and_1_out), .Q(d_ff_3_q));  // open: Qn, preset, reset
  and and_2 (b0, o, d_ff_1_q);
  and and_3 (b1, o, d_ff_2_q);
  and and_4 (b2, o, d_ff_3_q);

  // Notes on the sheet:
  //   Input
  //   1 = write
  //   0 = read
  //   Output
endmodule
